// Logisim project 567661_643594_T5.circ as structural Verilog: 1 circuit, main circuit main
module main (
  input  in_1,
  input  in_2,
  input  in_3,
  output out_4,
  output out_5,
  output out_6
);

  wire and_1_out, and_2_out, and_3_out, and_4_out, and_5_out, and_6_out, and_7_out, and_8_out, not_1_out,
       not_2_out, not_3_out, or_1_out, or_2_out, or_3_out;

  not not_1 (not_1_out, in_1);
  not not_2 (not_2_out, in_2);
  not not_3 (not_3_out, in_3);
  and and_1 (and_1_out, in_1, in_2);
  and and_2 (and_2_out, in_2, not_3_out);
  and and_3 (and_3_out, in_1, not_2_out);
  and and_4 (and_4_out, in_2, not_1_out, not_3_out);
  and and_5 (and_5_out, in_1, not_2_out, not_3_out);
  and and_6 (and_6_out, in_1, not_2_out, in_3);
  and and_7 (and_7_out, in_1, in_2, not_3_out);
  and and_8 (and_8_out, in_1, in_2, in_3);
  or or_1 (or_1_out, in_1, in_2, in_3);
  or or_2 (or_2_out, in_1, in_2, not_3_out);
  or or_3 (or_3_out, in_1, not_2_out, not_3_out);
  or or_4 (out_4, and_1_out, and_2_out, and_3_out);
  or or_5 (out_5, and_4_out, and_5_out, and_6_out, and_7_out, and_8_out);
  and and_9 (out_6, or_1_out, or_2_out, or_3_out);

  // Notes on the sheet:
  //   a       b       c
  //   ab
  //   bc'
  //   ab'
  //   Norma Elizondo Hubbard 567661
  //   Diego E. Garcia Horta 643594
  //   f(a,b,c) = ab + bc' + ab'
  //   SOP (minitérminos)
  //   POS (maxitérminos)
  //   Damos nuestra palabra de que hemos realizado esta actividad con integridad académica.
  //   Instrucciones: implementar la función y sus tres versiones (original, minitérminos y maxitérminos)
  //   f(a,b,c) = ab + bc' + ab'
  //   f(a,b,c) = Sumatoria m(2,4,5,6,7)
  //   f(a,b,c) = Multiplicatoria M(0,1,3)
  //   Maxitérminos o POS canónico
  //     = MULT M(      )
  //   Minitérminos o SOP canónico
  //    = SUMA m( 2,4,5,6,7 )  
  //   f(a,b,c) = ab + bc'+ ab'
endmodule
