// Logisim project Ejemplo2Clase.circ as structural Verilog: 1 circuit, main circuit main
module main (
  input  in_1,
  input  in_2,
  input  in_3,
  output out_4,
  output out_5,
  output out_6
);

  wire and_1_out, and_2_out, and_3_out, and_4_out, and_5_out, and_6_out, and_7_out, and_9_out, not_1_out,
       not_2_out, not_3_out, or_1_out, or_2_out, or_3_out, or_4_out, or_5_out, or_6_out;

  not not_1 (not_1_out, in_1);
  not not_2 (not_2_out, in_3);
  not not_3 (not_3_out, in_2);
  and and_1 (and_1_out, in_2, not_2_out);
  and and_2 (and_2_out, not_2_out, or_1_out);
  or or_1 (or_1_out, not_3_out, not_1_out);
  and and_3 (and_3_out, not_1_out, in_2);
  and and_4 (and_4_out, not_1_out, in_2, not_2_out);
  and and_5 (and_5_out, not_1_out, in_2, in_3);
  and and_6 (and_6_out, in_1, not_3_out, not_2_out);
  and and_7 (and_7_out, in_1, in_2, not_2_out);
  or or_2 (or_2_out, in_1, in_2, in_3);
  or or_3 (or_3_out, in_1, in_2, not_2_out);
  or or_4 (or_4_out, not_1_out, in_2, not_2_out);
  or or_5 (or_5_out, not_1_out, not_3_out, not_2_out);
  or or_6 (or_6_out, and_1_out, and_2_out);
  or or_7 (out_5, and_4_out, and_5_out, and_6_out, and_7_out);
  and and_8 (out_6, or_2_out, or_3_out, or_4_out, or_5_out);
  and and_9 (and_9_out, in_1, or_6_out);
  or or_8 (out_4, and_9_out, and_3_out);

  // Notes on the sheet:
  //   a       b       c
  //   c' (b' + a') 
  //   bc' + c' (b' + a')
  //   Minitérminos o SOP canónico
  //   Maxitérminos o POS canónico
  //    Ejemplo # 2 de los 2 ejemplos resueltos en clase
  //   a(bc' + c' (b' + a') )
  //    g(a,b,c) = a(bc' + c' (b' + a') ) + a'b
  //    = SUMA m( 2,3,4,6 )  
  //     = MULT M( 0,1,5,7 )
endmodule
