// Logisim project alarmaCinturonSeguridad.circ as structural Verilog: 1 circuit, main circuit main
module main (
  input  A,
  input  C,
  input  M,
  output out_4
);

  wire not_1_out, not_2_out, not_3_out;

  not not_1 (not_1_out, A);
  not not_2 (not_2_out, C);
  not not_3 (not_3_out, M);
  and and_1 (out_4, A, not_2_out, M);

  // Notes on the sheet:
  //   Alarma cinturon de seguridad
  //   A=1 asiento ocupado
  //   C=1 cinturon puesto
  //   M=1 motor encendido
endmodule
